# Fritzing sketch bt_door_unlock (saved by Fritzing 0.9.2b)
breadboards: 1

parts:
  Part1 = Arduino Uno (Rev3) - ICSP
  J1 = Basic Servo
  Part2 = Bluetooth Module Breakout - Roving Networks (RN-41)
  R1 = Resistor [tolerance=±5% resistance=220 package="2512 [SMD]"]
  VCC2 = 4 x AAA Battery Mount
  LED1 = smd LED [color="Red (633nm)" package="0603 [SMD]"]
  LED2 = smd LED [color="Red (633nm)" package="0603 [SMD]"]
  R2 = Resistor [tolerance=±5% resistance=220 package="2512 [SMD]"]
  R3 = Resistor [tolerance=±5% resistance=220 package="2512 [SMD]"]
  R4 = Resistor [tolerance=±5% resistance=220 package="2512 [SMD]"]
  R5 = Resistor [tolerance=±5% resistance=220 package="2512 [SMD]"]

nets:
  N1: Part1.A0, R4.Pin_0, R5.Pin_1
  N2: Part1.ICSP_MOSI, Part1.D11_PWM/MOSI, LED1.anode
  GND: Part1.GND, J1.gnd, Part2.GND, VCC2.-, R2.Pin_1, R3.Pin_1, R5.Pin_0
  N3: Part1.D10_PWM/SS, LED2.anode
  N4: Part1.D0/RX, Part2.UARTTX, R1.Pin_0
  N5: Part1.D1/TX, Part2.UARTRX
  N6: Part1.D2, R1.Pin_1
  N7: Part1.D3_PWM, J1.pulse
  3V3: Part1.3V3, Part2.VCC
  N8: Part1.5V, R4.Pin_1
  N9: J1.vcc, VCC2.+
  N10: LED1.cathode, R3.Pin_0
  N11: LED2.cathode, R2.Pin_0

// code stored in the sketch: bt_door_unlock_hw.ino

